# Fritzing sketch keybox (saved by Fritzing 0.9.3b)
breadboards: 1

parts:
  U1 = 74HC595 [package="DIP16 [THT]"]
  Mod1 = Raspberry Pi Pico
  R1 = Resistor [tolerance=±5% resistance=220 package=THT]
  LED1 = LED - 5mm [color="Red (633nm)" package="5 mm [THT]"]
  Reader_0 = RFID-RC522-v2
  Reader_1 = RFID-RC522-v2

nets:
  N1: U1.Q1, Reader_1.RST
  GND: U1.GND, U1.OE, LED1.cathode, Reader_0.GND, Reader_1.GND
  3.3V: U1.MR, U1.VCC, Reader_0.3.3V, Reader_1.3.3V
  N2: U1.SH_CP, Mod1.pin_10
  N3: U1.ST_CP, Mod1.pin_11
  N4: U1.DS, Mod1.pin_9
  N5: U1.Q0, Reader_0.RST
  SCK: Mod1.pin_4, Reader_0.SCK, Reader_1.SCK
  MOSI: Mod1.pin_5, Reader_0.MOSI, Reader_1.MOSI
  MISO: Mod1.pin_6, Reader_0.MISO, Reader_1.MISO
  SDA: Mod1.pin_7, Reader_0.SDA, Reader_1.SDA
  N6: Mod1.pin_21, R1.Pin_0
  N7: R1.Pin_1, LED1.anode

custom parts:
  Raspberry Pi Pico: Raspberry Pi Pico. Based around the RP2040 microcontroller the Pico is a low cost microcontroller device bringing Raspberry Pi quality, cost, and easy of use to the microcontroller space. Jan 2021, Split part in to two versions: tht (this one) and SMD. This one will drill holes for a .1 in header in pcb to allow plugging in the module as well as providing pads to solder the module to the top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
  RFID-RC522-v2: A simple China made RFID-RC522 Reader; do check the pin labels, as this is a MFRC522 based clone.
